# Fritzing sketch PCB-backup (saved by Fritzing 0.9.3b)
circuit board: 2.58228cm x 1.58514cm
breadboards: 1

parts:
  ATtiny13 = IC, DIP package, 8 pins [chip_label=Attiny spacing=300mil]
  RED = LED - 5mm [color="Red (633nm)" package="5 mm [THT]"]
  220Ω = Resistor [tolerance=±5% resistance=220 package=THT]
  220Ω_2 = Resistor [tolerance=±5% resistance=220 package=THT]
  1MΩ = Resistor [tolerance=±5% resistance=1M package=THT]
  IR = LED - 3mm [color="Infrared (940nm)" part_number=754-1600-nd package="3 mm [THT]"]
  IR_COL = LED - 5mm [color="Infrared (940nm)" package="5 mm [THT]"]
  PNP = PNP-Transistor [package="TO92 [THT]"]

nets:
  N1: ATtiny13.pin2, PNP.B
  N2: ATtiny13.pin3, ATtiny13.pin7, 1MΩ.Pin_0, IR_COL.anode
  N3: ATtiny13.pin4, 1MΩ.Pin_1
  N4: ATtiny13.pin5, RED.cathode
  N5: ATtiny13.pin8, IR.anode, IR_COL.cathode
  N6: RED.anode, 220Ω.Pin_1
  N7: 220Ω.Pin_0, PNP.E
  N8: 220Ω_2.Pin_0, PNP.C
  N9: 220Ω_2.Pin_1, IR.cathode
